// Logisim project CPU.circ as structural Verilog: 11 circuits, main circuit ARM_CPU_SINGLE
module ARM_CPU_SINGLE (
);

  wire clk, clr, control_unit_1_alusrc, control_unit_1_memtoreg, control_unit_1_memw, control_unit_1_pcsrc,
       control_unit_1_regw;
  wire [1:0] control_unit_1_alucontrol, control_unit_1_immsrc, control_unit_1_regsrc;
  wire [3:0] _3_0, _19_16, alu_1_alu_flags, cond, multiplexer_2_out, multiplexer_3_out;
  wire [5:4] Funct;
  wire [7:4] extender7_0;
  wire [11:8] extender11_0;
  wire [23:12] extender23_0;
  wire [27:26] IM;
  wire [31:0] adder_1_out, adder_2_out, alu_1_alu_result, data_memory_1_rd, extender_1_extout,
       multiplexer_1_out, multiplexer_4_out, multiplexer_5_out, register_1_q, register_file_1_rd1,
       register_file_1_rd2;

  Button u_clr (.out(clr));
  Clock clock_1 (.out(clk));
  Multiplexer #(.width(32), .enable("false")) multiplexer_1 (
    .in0(adder_1_out), .in1(multiplexer_5_out), .out(multiplexer_1_out), .sel(control_unit_1_pcsrc));
  Register #(.width(32)) register_1 (.D(multiplexer_1_out), .Q(register_1_q), .clk(clk), .clr(clr));  // open: en
  Adder #(.width(32)) adder_1 (.a(register_1_q), .b(32'h4), .out(adder_1_out));  // open: cin, cout
  ROM #(.dataWidth(32)) rom_1 (
    .addr(register_1_q[7:0]),
    .data({cond, IM, Funct, extender23_0[23:20], _19_16, extender23_0[15:12], extender11_0, extender7_0, _3_0}),
    .sel(1'b1));
  Multiplexer #(.width(4), .enable("false")) multiplexer_2 (
    .in0(_19_16), .in1(4'b1111), .out(multiplexer_2_out), .sel(control_unit_1_regsrc[0]));
  Adder #(.width(32)) adder_2 (.a(adder_1_out), .b(32'h4), .out(adder_2_out));  // open: cin, cout
  Control_Unit control_unit_1 (
    .Rd(extender23_0[15:12]), .Op(IM), .Funct({Funct, extender23_0[23:20]}), .Cond(cond),
    .ALUFlags(alu_1_alu_flags), .PCSrc(control_unit_1_pcsrc), .RegW(control_unit_1_regw),
    .MemW(control_unit_1_memw), .MemToReg(control_unit_1_memtoreg), .ALUSrc(control_unit_1_alusrc),
    .ImmSrc(control_unit_1_immsrc), .RegSrc(control_unit_1_regsrc), .ALUControl(control_unit_1_alucontrol),
    .clk(clk));
  Multiplexer #(.width(4), .enable("false")) multiplexer_3 (
    .in0(_3_0), .in1(extender23_0[15:12]), .out(multiplexer_3_out), .sel(control_unit_1_regsrc[1]));
  Register_File register_file_1 (
    .WD3(multiplexer_5_out), .clr(clr), .WE3(control_unit_1_regw), .RD1(register_file_1_rd1),
    .RD2(register_file_1_rd2), .A3(extender23_0[15:12]), .R15(adder_2_out), .A1(multiplexer_2_out),
    .A2(multiplexer_3_out), .clk(clk));
  extender extender_1 (
    .ImmSrc(control_unit_1_immsrc), .extender7_0({extender7_0, _3_0}),
    .extender11_0({extender11_0, extender7_0, _3_0}),
    .extender23_0({extender23_0[23:20], _19_16, extender23_0[15:12], extender11_0, extender7_0, _3_0}),
    .ExtOut(extender_1_extout));
  ALU alu_1 (
    .ALUControl(control_unit_1_alucontrol), .ALU_Flags(alu_1_alu_flags), .A(register_file_1_rd1),
    .B(multiplexer_4_out), .ALU_Result(alu_1_alu_result));
  Multiplexer #(.width(32), .enable("false")) multiplexer_4 (
    .in0(register_file_1_rd2), .in1(extender_1_extout), .out(multiplexer_4_out), .sel(control_unit_1_alusrc));
  Data_Memory data_memory_1 (
    .WE(control_unit_1_memw), .ALUResult(alu_1_alu_result), .WriteData(register_file_1_rd2), .CLR(clr),
    .RD(data_memory_1_rd), .CLK(clk));
  Multiplexer #(.width(32), .enable("false")) multiplexer_5 (
    .in0(alu_1_alu_result), .in1(data_memory_1_rd), .out(multiplexer_5_out), .sel(control_unit_1_memtoreg));

  // Other names for the same wires on the sheet: IM (some bits) = {cond, Funct, extender23_0[23:20], _19_16, extender23_0[15:12], extender11_0, extender7_0, _3_0};
  //   extender7_0[3:0] = _3_0; extender11_0[7:0] = {extender7_0, _3_0};
  //   extender23_0 (some bits) = {_19_16, extender11_0, extender7_0, _3_0}; Rd[3:0] = extender23_0[15:12];
  //   Funct[3:0] = extender23_0[23:20]; Op[1:0] = IM

  // Notes on the sheet:
  //   Instruction Memory
  //   31:28
  //   3:0
  //   contents of rom_1 (hex, n*v repeats v):
  //   e2506004 0 0 0 a000005 0 0 0 e5951000 0 0 0 e2811008 0 0 0 e5851000 0 0 0 e2855004 0 0 0 e2800001 0
  //   0 0 eafffff7 0 0 0 eafffffe
  //   PC plus4
  //   25:20
  //   27:26
  //   PC plus8
  //   19:16
  //   15:12
  //   23:0
  //   11:0
  //   7:0
  //   ALUResult
endmodule

module ALU (
  input  [31:0] A,
  input  [31:0] B,
  input  [1:0] ALUControl,
  output [31:0] ALU_Result,
  output [3:0] ALU_Flags
);

  wire adder_1_cout, not_1_out, or_2_out, subtractor_1_bout, xnor_1_out, xor_1_out;
  wire [31:0] adder_1_out, and_1_out, or_1_out, subtractor_1_out;

  Adder #(.width(32)) adder_1 (.a(B), .b(A), .out(adder_1_out), .cout(adder_1_cout));  // open: cin
  Subtractor #(.width(32)) subtractor_1 (.a(A), .b(B), .out(subtractor_1_out), .bout(subtractor_1_bout));  // open: bin
  assign and_1_out = B & A;  // AND_Gate and_1, 32 bits wide
  assign or_1_out = B | A;  // OR_Gate or_1, 32 bits wide
  Multiplexer #(.select(2), .width(32), .enable("false")) multiplexer_1 (
    .in0(adder_1_out), .in1(subtractor_1_out), .in2(and_1_out), .in3(or_1_out),
    .out({ALU_Flags[3], ALU_Result[30:0]}), .sel(ALUControl));
  Comparator #(.width(32)) comparator_1 (
    .a({ALU_Flags[3], ALU_Result[30:0]}), .b({32{1'b0}}), .eq(ALU_Flags[2]));  // open: gt, lt
  NotExactlyOne xnor_1 (.out(xnor_1_out), .in0(A[31]), .in1(B[31]), .in2(ALUControl[0]));
  not not_1 (not_1_out, ALUControl[1]);
  xor xor_1 (xor_1_out, B[31], adder_1_out[31]);
  and and_2 (ALU_Flags[1], xnor_1_out, xor_1_out, not_1_out);
  or or_2 (or_2_out, subtractor_1_bout, adder_1_cout);
  and and_3 (ALU_Flags[0], not_1_out, or_2_out);

  assign ALU_Result[31] = ALU_Flags[3];

  // Other names for the same wires on the sheet: C = ALU_Flags[0]; V = ALU_Flags[1]; Z = ALU_Flags[2];
  //   N = ALU_Flags[3]; ALU_Control_0 = ALUControl[0]; ALU_Control_1 = ALUControl[1]
endmodule

module Control_Unit (
  input  [3:0] Rd,
  input  [1:0] Op,
  input  [5:0] Funct,
  input  [3:0] Cond,
  input  [3:0] ALUFlags,
  input  clk,
  output PCSrc,
  output RegW,
  output MemW,
  output MemToReg,
  output ALUSrc,
  output [1:0] ImmSrc,
  output [1:0] RegSrc,
  output [1:0] ALUControl
);

  wire bit_extender_1_out, decoder_1_memw, decoder_1_pcs, decoder_1_regw;
  wire [1:0] and_1_out, decoder_1_flagw, register_1_q, register_2_q, undriven;

  Decoder decoder_1 (
    .Rd3_0(Rd), .Op1_0(Op), .funct5_0(Funct), .PCS(decoder_1_pcs), .RegW(decoder_1_regw),
    .MemW(decoder_1_memw), .MemToReg(MemToReg), .ALUSrc(ALUSrc), .ImmSrc(ImmSrc), .RegSrc(RegSrc),
    .ALUControl(ALUControl), .FlagW(decoder_1_flagw));
  Register #(.width(2)) register_1 (.D(ALUFlags[3:2]), .Q(register_1_q), .clk(clk), .clr(and_1_out[1]));  // open: en
  Register #(.width(2)) register_2 (.D(ALUFlags[1:0]), .Q(register_2_q), .clk(clk), .clr(and_1_out[0]));  // open: en
  assign and_1_out = decoder_1_flagw & undriven;  // AND_Gate and_1, 2 bits wide
  Bit_Extender #(.in_width(2), .out_width(1)) bit_extender_1 (.in(undriven), .out(bit_extender_1_out));
  condition_check condition_check_1 (.Cond(Cond), .ALUFlags({register_1_q, register_2_q}), .CondEx(bit_extender_1_out));
  and and_2 (PCSrc, decoder_1_pcs, bit_extender_1_out);
  and and_3 (RegW, decoder_1_regw, bit_extender_1_out);
  and and_4 (MemW, decoder_1_memw, bit_extender_1_out);
endmodule

module Data_Memory (
  input  WE,
  input  [31:0] ALUResult,
  input  [31:0] WriteData,
  input  CLR,
  input  CLK,
  output [31:0] RD
);

  wire not_1_out;

  RAM #(.dataWidth(32), .bus("separate")) ram_1 (
    .addr(ALUResult[9:2]), .din(WriteData), .data(RD), .str(WE), .clk(CLK), .ld(not_1_out), .clr(CLR));  // open: sel
  not not_1 (not_1_out, WE);
endmodule

module Register_File (
  input  [31:0] WD3,
  input  clk,
  input  clr,
  input  [3:0] A1,
  input  [3:0] A2,
  input  [31:0] R15,
  input  WE3,
  input  [3:0] A3,
  output [31:0] RD1,
  output [31:0] RD2
);

  wire decoder_1_out0, decoder_1_out1, decoder_1_out2, decoder_1_out3, decoder_1_out4, decoder_1_out5,
       decoder_1_out6, decoder_1_out7, decoder_1_out8, decoder_1_out9, decoder_1_out10, decoder_1_out11,
       decoder_1_out12, decoder_1_out13, decoder_1_out14;
  wire [31:0] R0_q, R1_q, R2_q, R3_q, R4_q, R5_q, R6_q, R7_q, R8_q, R9_q, R10_q, R11_q, R12_q, R13_q, R14_q;

  Decoder_part #(.select(4), .disabled(0)) decoder_1 (
    .out0(decoder_1_out0), .out1(decoder_1_out1), .out2(decoder_1_out2), .out3(decoder_1_out3),
    .out4(decoder_1_out4), .out5(decoder_1_out5), .out6(decoder_1_out6), .out7(decoder_1_out7),
    .out8(decoder_1_out8), .out9(decoder_1_out9), .out10(decoder_1_out10), .out11(decoder_1_out11),
    .out12(decoder_1_out12), .out13(decoder_1_out13), .out14(decoder_1_out14), .sel(A3), .en(WE3));  // open: out15
  Register #(.width(32)) R14 (.D(WD3), .en(decoder_1_out14), .Q(R14_q), .clk(clk), .clr(clr));
  Register #(.width(32)) R13 (.D(WD3), .en(decoder_1_out13), .Q(R13_q), .clk(clk), .clr(clr));
  Register #(.width(32)) R11 (.D(WD3), .en(decoder_1_out11), .Q(R11_q), .clk(clk), .clr(clr));
  Register #(.width(32)) R12 (.D(WD3), .en(decoder_1_out12), .Q(R12_q), .clk(clk), .clr(clr));
  Register #(.width(32)) R10 (.D(WD3), .en(decoder_1_out10), .Q(R10_q), .clk(clk), .clr(clr));
  Register #(.width(32)) R9 (.D(WD3), .en(decoder_1_out9), .Q(R9_q), .clk(clk), .clr(clr));
  Register #(.width(32)) R8 (.D(WD3), .en(decoder_1_out8), .Q(R8_q), .clk(clk), .clr(clr));
  Register #(.width(32)) R7 (.D(WD3), .en(decoder_1_out7), .Q(R7_q), .clk(clk), .clr(clr));
  Register #(.width(32)) R6 (.D(WD3), .en(decoder_1_out6), .Q(R6_q), .clk(clk), .clr(clr));
  Register #(.width(32)) R5 (.D(WD3), .en(decoder_1_out5), .Q(R5_q), .clk(clk), .clr(clr));
  Register #(.width(32)) R3 (.D(WD3), .en(decoder_1_out3), .Q(R3_q), .clk(clk), .clr(clr));
  Register #(.width(32)) R4 (.D(WD3), .en(decoder_1_out4), .Q(R4_q), .clk(clk), .clr(clr));
  Register #(.width(32)) R2 (.D(WD3), .en(decoder_1_out2), .Q(R2_q), .clk(clk), .clr(clr));
  Register #(.width(32)) R1 (.D(WD3), .en(decoder_1_out1), .Q(R1_q), .clk(clk), .clr(clr));
  Register #(.width(32)) R0 (.D(WD3), .en(decoder_1_out0), .Q(R0_q), .clk(clk), .clr(clr));
  Multiplexer #(.select(4), .width(32), .enable("false")) multiplexer_1 (
    .in0(R0_q), .in1(R1_q), .in2(R2_q), .in3(R3_q), .in4(R4_q), .in5(R5_q), .in6(R6_q), .in7(R7_q),
    .in8(R8_q), .in9(R9_q), .in10(R10_q), .in11(R11_q), .in12(R12_q), .in13(R13_q), .in14(R14_q), .in15(R15),
    .out(RD1), .sel(A1));
  Multiplexer #(.select(4), .width(32), .enable("false")) multiplexer_2 (
    .in0(R0_q), .in1(R1_q), .in2(R2_q), .in3(R3_q), .in4(R4_q), .in5(R5_q), .in6(R6_q), .in7(R7_q),
    .in8(R8_q), .in9(R9_q), .in10(R10_q), .in11(R11_q), .in12(R12_q), .in13(R13_q), .in14(R14_q), .out(RD2),
    .sel(A2));  // open: in15
endmodule

module ALUDecoder (
  input  ALUop,
  input  [5:0] Func,
  output [1:0] ALUCont,
  output [1:0] FlagW
);

  wire and_1_out, or_1_out, or_2_out;

  or or_1 (or_1_out, Func[4], and_1_out);
  and and_1 (and_1_out, ~Func[2], ~Func[3]);  // AND_Gate
  or or_2 (or_2_out, Func[4], Func[2]);
  and and_2 (ALUCont[1], ALUop, or_1_out);
  and and_3 (ALUCont[0], ALUop, or_2_out);
  and and_4 (FlagW[1], ALUop, Func[0]);
  and and_5 (FlagW[0], FlagW[1], ~ALUCont[1]);  // AND_Gate
endmodule

module MainDecoder (
  input  [1:0] Op_1_0,
  input  [5:0] Func_5_0,
  output Branch,
  output RegW,
  output MemW,
  output MemToReg,
  output ALUSrc,
  output [1:0] ImmSrc,
  output [1:0] RegSrc,
  output ALUOp
);

  wire or_2_out;

  and and_1 (ALUOp, ~Op_1_0[1], ~Op_1_0[0]);  // AND_Gate
  and and_2 (MemW, Op_1_0[0], ~Func_5_0[0]);  // AND_Gate
  or or_1 (ALUSrc, Func_5_0[5], Op_1_0[0], Op_1_0[1]);
  and and_3 (RegW, ~Op_1_0[1], or_2_out);  // AND_Gate
  or or_2 (or_2_out, Func_5_0[0], ~Op_1_0[0]);  // OR_Gate

  assign Branch = Op_1_0[1];
  assign ImmSrc = Op_1_0;
  assign MemToReg = Op_1_0[0];
  assign RegSrc = {Op_1_0[0], Op_1_0[1]};

  // Other names for the same wires on the sheet: F0 = Func_5_0[0]; F1 = Func_5_0[1]; F2 = Func_5_0[2];
  //   F3 = Func_5_0[3]; F4 = Func_5_0[4]; F5 = Func_5_0[5]; Op1 = Op_1_0[1]; Op0 = Op_1_0[0]
endmodule

module condition_check (
  input  [3:0] Cond,
  input  [3:0] ALUFlags,
  output CondEx
);

  wire and_1_out, and_2_out, and_3_out;

  and and_1 (and_1_out, ~Cond[0], Cond[1], Cond[2], Cond[3]);  // AND_Gate
  and and_2 (and_2_out, ~Cond[0], ~Cond[1], ~Cond[2], ~Cond[3], ALUFlags[2]);  // AND_Gate
  and and_3 (and_3_out, Cond[0], ~Cond[1], ~Cond[2], ~Cond[3], ~ALUFlags[2]);  // AND_Gate
  or or_1 (CondEx, and_1_out, and_2_out, and_3_out);
endmodule

module PC_Logic (
  input  [3:0] Rd,
  input  RegW,
  input  Branch,
  output PCS
);

  wire and_1_out;

  and and_1 (and_1_out, Rd[0], Rd[1], Rd[2], Rd[3], RegW);
  or or_1 (PCS, and_1_out, Branch);
endmodule

module Decoder (
  input  [3:0] Rd3_0,
  input  [1:0] Op1_0,
  input  [5:0] funct5_0,
  output PCS,
  output RegW,
  output MemW,
  output MemToReg,
  output ALUSrc,
  output [1:0] ImmSrc,
  output [1:0] RegSrc,
  output [1:0] ALUControl,
  output [1:0] FlagW
);

  wire maindecoder_1_aluop, maindecoder_1_branch;

  MainDecoder maindecoder_1 (
    .Op_1_0(Op1_0), .Func_5_0(funct5_0), .Branch(maindecoder_1_branch), .RegW(RegW), .MemW(MemW),
    .MemToReg(MemToReg), .ALUSrc(ALUSrc), .ImmSrc(ImmSrc), .RegSrc(RegSrc), .ALUOp(maindecoder_1_aluop));
  ALUDecoder aludecoder_1 (.ALUop(maindecoder_1_aluop), .Func(funct5_0), .ALUCont(ALUControl), .FlagW(FlagW));
  PC_Logic pc_logic_1 (.RegW(RegW), .Branch(maindecoder_1_branch), .PCS(PCS), .Rd(Rd3_0));
endmodule

module extender (
  input  [7:0] extender7_0,
  input  [1:0] ImmSrc,
  input  [11:0] extender11_0,
  input  [23:0] extender23_0,
  output [31:0] ExtOut
);

  wire [31:0] bit_extender_1_out, bit_extender_2_out, bit_extender_3_out, multiplier_1_out;

  assign bit_extender_1_out = {{24{1'b0}}, extender7_0};  // Bit_Extender bit_extender_1
  assign bit_extender_2_out = {{20{1'b0}}, extender11_0};  // Bit_Extender bit_extender_2
  assign bit_extender_3_out = {{8{extender23_0[23]}}, extender23_0};  // Bit_Extender bit_extender_3
  Multiplexer #(.select(2), .width(32), .enable("false")) multiplexer_1 (
    .in0(bit_extender_1_out), .in1(bit_extender_2_out), .in2(multiplier_1_out), .out(ExtOut), .sel(ImmSrc));  // open: in3
  Multiplier #(.width(32)) multiplier_1 (.a(bit_extender_3_out), .b(32'h4), .out(multiplier_1_out));  // open: cin, cout
endmodule
