// Logisim project ShafahatSardarov-ALUDecoder.circ as structural Verilog: 1 circuit, main circuit main
module main (
  input  ALUOp,
  input  [5:0] Funct_5_0,
  output [1:0] FlagW_1_0,
  output [1:0] ALUControl_1_0
);

  wire _00000_out, _00001_out, _00100_out, _00101_out, _01001_out, _11000_out, _11001_out, C1_out, C2_out,
       W1_out, W2_out;

  and _01001 (_01001_out, Funct_5_0[0], ~Funct_5_0[1], ~Funct_5_0[2], Funct_5_0[3], ~Funct_5_0[4]);  // AND_Gate
  and _00100 (_00100_out, ~Funct_5_0[0], ~Funct_5_0[1], Funct_5_0[2], ~Funct_5_0[3], ~Funct_5_0[4]);  // AND_Gate
  and _00101 (_00101_out, Funct_5_0[0], ~Funct_5_0[1], Funct_5_0[2], ~Funct_5_0[3], ~Funct_5_0[4]);  // AND_Gate
  and _00000 (_00000_out, ~Funct_5_0[0], ~Funct_5_0[1], ~Funct_5_0[2], ~Funct_5_0[3], ~Funct_5_0[4]);  // AND_Gate
  and _00001 (_00001_out, Funct_5_0[0], ~Funct_5_0[1], ~Funct_5_0[2], ~Funct_5_0[3], ~Funct_5_0[4]);  // AND_Gate
  and _11000 (_11000_out, ~Funct_5_0[0], ~Funct_5_0[1], ~Funct_5_0[2], Funct_5_0[3], Funct_5_0[4]);  // AND_Gate
  and _11001 (_11001_out, Funct_5_0[0], ~Funct_5_0[1], ~Funct_5_0[2], Funct_5_0[3], Funct_5_0[4]);  // AND_Gate
  or W1 (W1_out, _01001_out, _00101_out, _00001_out, _11001_out);
  or W2 (W2_out, _01001_out, _00101_out);
  or C2 (C2_out, _00100_out, _00101_out, _11000_out, _11001_out);
  or C1 (C1_out, _00000_out, _00001_out, _11000_out, _11001_out);
  and and_1 (FlagW_1_0[1], W1_out, ALUOp);
  and and_2 (FlagW_1_0[0], W2_out, ALUOp);
  and and_3 (ALUControl_1_0[0], C2_out, ALUOp);
  and and_4 (ALUControl_1_0[1], C1_out, ALUOp);
endmodule
