// Logisim project ShafahatSardarov_MainDecoder.circ as structural Verilog
// Data Memory
module DataMemory (
  input  WE,
  input  [31:0] ALUResult,
  input  [31:0] WriteData,
  input  CLR,
  input  CLK,
  output [31:0] out_6
);

  wire not_1_out;

  RAM #(.dataWidth(32), .bus("separate")) ram_1 (
    .addr(ALUResult[9:2]), .din(WriteData), .data(out_6), .str(WE), .clk(CLK), .ld(not_1_out), .clr(CLR));  // open: sel
  not not_1 (not_1_out, WE);
endmodule
